# Fritzing sketch Schaltplan (saved by Fritzing 1.0.3b)
breadboards: 1

parts:
  Raspberry_Pi1 = Raspberry Pi 2
  RHT1 = Humidity and Temperature Sensor RHT03

nets:
  N1: Raspberry_Pi1.GPIO4, RHT1.Data-signal
  N2: Raspberry_Pi1.GND, RHT1.GND_1
